// Logisim project TermProject.circ as structural Verilog
module FullAdder (
  input  A,
  input  B,
  input  Cin,
  output S,
  output Cout
);

  wire and_1_out, and_2_out, xor_1_out;

  xor xor_1 (xor_1_out, A, B);
  xor xor_2 (S, xor_1_out, Cin);
  and and_1 (and_1_out, xor_1_out, Cin);
  and and_2 (and_2_out, A, B);
  or or_1 (Cout, and_1_out, and_2_out);
endmodule

module Complement (
  input  [7:0] In,
  input  B,
  input  Cin,
  output [7:0] X
);

  wire fulladder_1_cout, fulladder_2_cout, fulladder_3_cout, fulladder_4_cout, fulladder_5_cout,
       fulladder_6_cout, fulladder_7_cout;
  wire [7:0] not_1_out;

  assign not_1_out = ~In;  // NOT_Gate not_1, 8 bits wide
  FullAdder fulladder_1 (.A(not_1_out[0]), .B(B), .Cin(Cin), .S(X[0]), .Cout(fulladder_1_cout));
  FullAdder fulladder_2 (.A(not_1_out[1]), .B(B), .Cin(fulladder_1_cout), .S(X[1]), .Cout(fulladder_2_cout));
  FullAdder fulladder_3 (.A(not_1_out[2]), .B(B), .Cin(fulladder_2_cout), .S(X[2]), .Cout(fulladder_3_cout));
  FullAdder fulladder_4 (.A(not_1_out[3]), .B(B), .Cin(fulladder_3_cout), .S(X[3]), .Cout(fulladder_4_cout));
  FullAdder fulladder_5 (.A(not_1_out[4]), .B(B), .Cin(fulladder_4_cout), .S(X[4]), .Cout(fulladder_5_cout));
  FullAdder fulladder_6 (.A(not_1_out[5]), .B(B), .Cin(fulladder_5_cout), .S(X[5]), .Cout(fulladder_6_cout));
  FullAdder fulladder_7 (.A(not_1_out[6]), .B(B), .Cin(fulladder_6_cout), .S(X[6]), .Cout(fulladder_7_cout));
  FullAdder fulladder_8 (.A(not_1_out[7]), .Cin(fulladder_7_cout), .S(X[7]));  // open: B, Cout
endmodule

module rotl (
  input  [7:0] A,
  input  [2:0] B,
  output [7:0] O1
);

  Multiplexer #(.select(3), .width(8)) multiplexer_1 (
    .in0(A), .in1({A[6:0], A[7]}), .in2({A[5:0], A[7:6]}), .in3({A[4:0], A[7:5]}), .in4({A[3:0], A[7:4]}),
    .in5({A[2:0], A[7:3]}), .in6({A[1:0], A[7:2]}), .in7({A[0], A[7:1]}), .out(O1), .sel(B));

  // Other names for the same wires on the sheet: amount[2:0] = B; first = A[1]; O0[7:0] = A;
  //   O1_t[7:0] = {A[6:0], A[7]}; O2[7:0] = {A[5:0], A[7:6]}; O3[7:0] = {A[4:0], A[7:5]}; O4[7:0] = {A[3:0], A[7:4]};
  //   O5[7:0] = {A[2:0], A[7:3]}; O6[7:0] = {A[1:0], A[7:2]}; O7[7:0] = {A[0], A[7:1]}; sec = A[2]; third = A[3];
  //   fourth = A[4]; fifth = A[5]; sixth = A[6]; seventh = A[7]; zero = A[0]
endmodule

module twoscomplement (
  input  [7:0] In,
  input  B,
  input  Cin,
  output O1,
  output [7:0] O2
);

  Complement complement_1 (.In(In), .B(B), .Cin(Cin), .X(O2));
  and and_1 (O1, In[0], In[7]);
endmodule

module FADDER8 (
  input  [7:0] B,
  input  [7:0] A,
  input  Cin,
  output [7:0] SUM,
  output Cout
);

  wire fulladder_1_cout, fulladder_2_cout, fulladder_3_cout, fulladder_4_cout, fulladder_5_cout,
       fulladder_6_cout, fulladder_7_cout;

  FullAdder fulladder_1 (.A(A[0]), .B(B[0]), .Cin(Cin), .S(SUM[0]), .Cout(fulladder_1_cout));
  FullAdder fulladder_2 (.A(A[1]), .B(B[1]), .Cin(fulladder_1_cout), .S(SUM[1]), .Cout(fulladder_2_cout));
  FullAdder fulladder_3 (.A(A[2]), .B(B[2]), .Cin(fulladder_2_cout), .S(SUM[2]), .Cout(fulladder_3_cout));
  FullAdder fulladder_4 (.A(A[3]), .B(B[3]), .Cin(fulladder_3_cout), .S(SUM[3]), .Cout(fulladder_4_cout));
  FullAdder fulladder_5 (.A(A[4]), .B(B[4]), .Cin(fulladder_4_cout), .S(SUM[4]), .Cout(fulladder_5_cout));
  FullAdder fulladder_6 (.A(A[5]), .B(B[5]), .Cin(fulladder_5_cout), .S(SUM[5]), .Cout(fulladder_6_cout));
  FullAdder fulladder_7 (.A(A[6]), .B(B[6]), .Cin(fulladder_6_cout), .S(SUM[6]), .Cout(fulladder_7_cout));
  FullAdder fulladder_8 (.A(A[7]), .B(B[7]), .Cin(fulladder_7_cout), .S(SUM[7]), .Cout(Cout));

  // Other names for the same wires on the sheet: S0 = SUM[0]; S1 = SUM[1]; S2 = SUM[2]; S3 = SUM[3]; S4 = SUM[4];
  //   S5 = SUM[5]; S6 = SUM[6]; S7 = SUM[7]
endmodule

module ALU8 (
  input  [7:0] A,
  input  [7:0] B,
  input  Cin,
  input  [1:0] opcode,
  output [7:0] result
);

  wire Cout;
  wire [7:0] ANDr, ORr, SUM;

  assign ANDr = A & B;  // AND_Gate and_1, 8 bits wide
  assign ORr = A | B;  // OR_Gate or_1, 8 bits wide
  FADDER8 fadder8_1 (.B(B), .A(A), .Cin(Cin), .SUM(SUM), .Cout(Cout));
  Multiplexer #(.select(2), .width(8)) multiplexer_1 (
    .in0(SUM), .in1(ANDr), .in2(ORr), .out(result), .sel(opcode));  // open: in3
endmodule

module rotr (
  input  [7:0] A,
  input  [2:0] B,
  output [7:0] O1
);

  Multiplexer #(.select(3), .width(8)) multiplexer_1 (
    .in0(A), .in1({A[0], A[7:1]}), .in2({A[1:0], A[7:2]}), .in3({A[2:0], A[7:3]}), .in4({A[3:0], A[7:4]}),
    .in5({A[4:0], A[7:5]}), .in6({A[5:0], A[7:6]}), .in7({A[6:0], A[7]}), .out(O1), .sel(B));

  // Other names for the same wires on the sheet: amount[2:0] = B; O0[7:0] = A; O1_t[7:0] = {A[0], A[7:1]};
  //   O2[7:0] = {A[1:0], A[7:2]}; O3[7:0] = {A[2:0], A[7:3]}; O4[7:0] = {A[3:0], A[7:4]}; O5[7:0] = {A[4:0], A[7:5]};
  //   O6[7:0] = {A[5:0], A[7:6]}; O7[7:0] = {A[6:0], A[7]}; seventh = A[7]; zero = A[0]; first = A[1]; sec = A[2];
  //   third = A[3]; fourth = A[4]; fifth = A[5]; sixth = A[6]
endmodule
