// Logisim project BerkeDiler_240150.circ as structural Verilog: 7 circuits, main circuit ALU8
// ALU
module ALU8 (
  input  [7:0] X,
  input  [7:0] Y,
  input  [1:0] ALUfunc,
  output [7:0] RESULT
);

  wire [7:0] adder_1_out, and_1_out, or_1_out, shifter_1_out;

  Adder adder_1 (.a(X), .b(Y), .out(adder_1_out));  // open: cin, cout
  Shifter #(.shift("rl")) shifter_1 (.in(X), .\dist (Y[2:0]), .out(shifter_1_out));
  assign and_1_out = X & Y;  // AND_Gate and_1, 8 bits wide
  assign or_1_out = X | Y;  // OR_Gate or_1, 8 bits wide
  Multiplexer #(.select(2), .width(8)) multiplexer_1 (
    .in0(adder_1_out), .in1(and_1_out), .in2(or_1_out), .in3(shifter_1_out), .out(RESULT), .sel(ALUfunc));
endmodule

// Register File
module Register_File (
  input  [2:0] rs,
  input  [2:0] rt,
  input  [2:0] rd,
  input  WE,
  input  [7:0] Data,
  input  CLK,
  output [7:0] read_data1,
  output [7:0] read_data2
);

  wire decoder_1_out0, decoder_1_out1, decoder_1_out2, decoder_1_out3, decoder_1_out4, decoder_1_out5,
       decoder_1_out6, decoder_1_out7;
  wire [7:0] register_1_q, register_2_q, register_3_q, register_4_q, register_5_q, register_6_q,
       register_7_q, register_8_q;

  Decoder #(.select(3)) decoder_1 (
    .out0(decoder_1_out0), .out1(decoder_1_out1), .out2(decoder_1_out2), .out3(decoder_1_out3),
    .out4(decoder_1_out4), .out5(decoder_1_out5), .out6(decoder_1_out6), .out7(decoder_1_out7), .sel(rd),
    .en(WE));
  Register #(.trigger("falling")) register_1 (.D(Data), .en(decoder_1_out0), .clk(CLK), .Q(register_1_q));  // open: clr
  Register #(.trigger("falling")) register_2 (.D(Data), .en(decoder_1_out1), .clk(CLK), .Q(register_2_q));  // open: clr
  Register #(.trigger("falling")) register_3 (.D(Data), .en(decoder_1_out2), .clk(CLK), .Q(register_3_q));  // open: clr
  Register #(.trigger("falling")) register_4 (.D(Data), .en(decoder_1_out3), .clk(CLK), .Q(register_4_q));  // open: clr
  Register #(.trigger("falling")) register_5 (.D(Data), .en(decoder_1_out4), .clk(CLK), .Q(register_5_q));  // open: clr
  Register #(.trigger("falling")) register_6 (.D(Data), .en(decoder_1_out5), .clk(CLK), .Q(register_6_q));  // open: clr
  Register #(.trigger("falling")) register_7 (.D(Data), .en(decoder_1_out6), .clk(CLK), .Q(register_7_q));  // open: clr
  Register #(.trigger("falling")) register_8 (.D(Data), .en(decoder_1_out7), .clk(CLK), .Q(register_8_q));  // open: clr
  Multiplexer #(.select(3), .width(8)) multiplexer_1 (
    .in0(register_1_q), .in1(register_2_q), .in2(register_3_q), .in3(register_4_q), .in4(register_5_q),
    .in5(register_6_q), .in6(register_7_q), .in7(register_8_q), .out(read_data1), .sel(rs));
  Multiplexer #(.select(3), .width(8)) multiplexer_2 (
    .in0(register_1_q), .in1(register_2_q), .in2(register_3_q), .in3(register_4_q), .in4(register_5_q),
    .in5(register_6_q), .in6(register_7_q), .in7(register_8_q), .out(read_data2), .sel(rt));
endmodule

module CPU (
  input  in_1,
  output [3:0] out_2,
  output [2:0] out_3,
  output [7:0] out_4,
  output [7:0] out_5,
  output [2:0] out_6,
  output [2:0] out_7,
  output [20:0] out_8,
  output [9:0] out_9,
  output [7:0] out_10
);

  wire clock_1_out, MR, mux2, MW, WE;
  wire [1:0] alufunc, mux1;
  wire [7:0] Data_Mem_readdata, multiplexer_1_out, multiplexer_2_out, Reg_File_read_data2;

  Clock clock_1 (.out(clock_1_out));
  ProgramCounter PC (.Clock(clock_1_out), .ResetPC(in_1), .PC(out_9));
  Control_Unit control_unit_1 (.Opcode(out_2), .mux1(mux1), .mux2(mux2), .WE(WE), .MW(MW), .MR(MR), .alufunc(alufunc));
  Instruction_Memory Ins_Memory (.In(out_9), .Ins_Mem_Out({out_2, out_3, out_6, out_7, out_8[7:0]}));
  Multiplexer #(.select(2), .width(8)) multiplexer_1 (
    .in0(out_4), .in1(Data_Mem_readdata), .in2(out_8[7:0]), .out(multiplexer_1_out), .sel(mux1));  // open: in3
  Register_File Reg_File (
    .rs(out_3), .rt(out_6), .rd(out_7), .WE(WE), .Data(multiplexer_1_out), .CLK(clock_1_out),
    .read_data1(out_5), .read_data2(Reg_File_read_data2));
  Multiplexer #(.width(8)) multiplexer_2 (
    .in0(Reg_File_read_data2), .in1(out_8[7:0]), .out(multiplexer_2_out), .sel(mux2));
  ALU8 ALU_8 (.X(out_5), .Y(multiplexer_2_out), .ALUfunc(alufunc), .RESULT(out_4));
  Data_Memory Data_Mem (
    .Address(out_4), .WE(MW), .RE(MR), .Clock(clock_1_out), .Data(Reg_File_read_data2),
    .ReadData(Data_Mem_readdata));

  assign out_8[20:8] = {out_2, out_3, out_6, out_7};
  assign out_10 = out_8[7:0];

  // Notes on the sheet:
  //   immediate
  //   opcode
  //   immediate
  //   ALU result
endmodule

module Instruction_Memory (
  input  [9:0] In,
  output [20:0] Ins_Mem_Out
);

  ROM #(.addrWidth(10), .dataWidth(21)) rom_1 (.addr(In), .data(Ins_Mem_Out));

  // Notes on the sheet:
  //   contents of rom_1 (hex, n*v repeats v):
  //   60108 60204 88b00 8c00 188d00 44300 67000
endmodule

// PC
module ProgramCounter (
  input  Clock,
  input  ResetPC,
  output [9:0] PC
);

  wire [9:0] adder_1_out;

  Register #(.trigger("falling"), .width(10)) register_1 (
    .D(adder_1_out), .clk(Clock), .Q(PC), .clr(ResetPC));  // open: en
  Adder #(.width(10)) adder_1 (.a(PC), .b(10'h1), .out(adder_1_out));  // open: cin, cout
endmodule

module Data_Memory (
  input  [7:0] Address,
  input  WE,
  input  RE,
  input  Clock,
  input  [7:0] Data,
  output [7:0] ReadData
);

  RAM #(.asyncread("true"), .trigger("falling")) ram_data (
    .addr(Address), .we(WE), .oe(RE), .clk(Clock), .din(Data), .dout(ReadData));
endmodule

module Control_Unit (
  input  [3:0] Opcode,
  output [1:0] mux1,
  output mux2,
  output WE,
  output MW,
  output MR,
  output [1:0] alufunc
);

  wire not_1_out, not_2_out, not_3_out, not_4_out;

  not not_1 (not_1_out, Opcode[1]);
  not not_2 (not_2_out, Opcode[1]);
  not not_3 (not_3_out, Opcode[0]);
  not not_4 (not_4_out, Opcode[1]);
  and mux1_0 (mux1[0], not_1_out, Opcode[0]);
  and mux1_1 (mux1[1], Opcode[1], Opcode[0]);
  or mux2_0 (mux2, Opcode[1], Opcode[0]);
  or WE_0 (WE, not_2_out, Opcode[0]);
  and and_1 (MW, Opcode[1], not_3_out);
  and and_2 (MR, not_4_out, Opcode[0]);

  assign alufunc = Opcode[3:2];

  // Other names for the same wires on the sheet: op2 = Opcode[2]; op3 = Opcode[3]; op0 = Opcode[0]; op1 = Opcode[1]
endmodule
