// Logisim project ALU__8.circ as structural Verilog: 1 circuit, main circuit ALU8
// ALU
module ALU8 (
  input  [7:0] X,
  input  [7:0] Y,
  input  [1:0] ALUfunc,
  output [7:0] RESULT
);

  wire clock_1_out;
  wire [7:0] adder_1_out, and_1_out, or_1_out, shifter_1_out;

  Clock clock_1 (.out(clock_1_out));
  Register register_1 (.clk(clock_1_out));  // open: D, en, Q, clr
  RAM ram_1 (.clk(clock_1_out));  // open: addr, we, oe, din, dout
  Adder adder_1 (.a(X), .b(Y), .out(adder_1_out));  // open: cin, cout
  Shifter #(.shift("rl")) shifter_1 (.in(X), .\dist (Y[2:0]), .out(shifter_1_out));
  assign and_1_out = X & Y;  // AND_Gate and_1, 8 bits wide
  assign or_1_out = X | Y;  // OR_Gate or_1, 8 bits wide
  Multiplexer #(.select(2), .width(8)) multiplexer_1 (
    .in0(adder_1_out), .in1(and_1_out), .in2(or_1_out), .in3(shifter_1_out), .out(RESULT), .sel(ALUfunc));
endmodule
