// Logisim project BerkeDiler_240150.circ as structural Verilog
// ALU
module ALU8 (
  input  [7:0] X,
  input  [7:0] Y,
  input  [2:0] ALUfunc,
  output [7:0] RESULT,
  output EQ
);

  wire [0:0] comparator_1_lt;
  wire [7:0] adder_1_out, and_1_out, or_1_out, shifter_1_out;

  Comparator comparator_1 (.a(X), .b(Y), .eq(EQ), .lt(comparator_1_lt[0]));  // open: gt
  Adder adder_1 (.a(X), .b(Y), .out(adder_1_out));  // open: cin, cout
  Shifter #(.shift("rl")) shifter_1 (.in(X), .\dist (Y[2:0]), .out(shifter_1_out));
  assign and_1_out = X & Y;  // AND_Gate and_1, 8 bits wide
  assign or_1_out = X | Y;  // OR_Gate or_1, 8 bits wide
  Multiplexer #(.select(3), .width(8)) multiplexer_1 (
    .in0(adder_1_out), .in1(and_1_out), .in2(or_1_out), .in3(shifter_1_out),
    .in4({{7{1'b0}}, comparator_1_lt[0]}), .out(RESULT), .sel(ALUfunc));  // open: in5, in6, in7
endmodule

// Register File
module Register_File (
  input  [2:0] rs,
  input  [2:0] rt,
  input  [2:0] rd,
  input  WE,
  input  [7:0] Data,
  input  CLK,
  output [7:0] read_data1,
  output [7:0] read_data2
);

  wire decoder_1_out0, decoder_1_out1, decoder_1_out2, decoder_1_out3, decoder_1_out4, decoder_1_out5,
       decoder_1_out6, decoder_1_out7;
  wire [7:0] register_1_q, register_2_q, register_3_q, register_4_q, register_5_q, register_6_q,
       register_7_q, register_8_q;

  Decoder #(.select(3)) decoder_1 (
    .out0(decoder_1_out0), .out1(decoder_1_out1), .out2(decoder_1_out2), .out3(decoder_1_out3),
    .out4(decoder_1_out4), .out5(decoder_1_out5), .out6(decoder_1_out6), .out7(decoder_1_out7), .sel(rd),
    .en(WE));
  Register #(.trigger("falling")) register_1 (.D(Data), .en(decoder_1_out0), .clk(CLK), .Q(register_1_q));  // open: clr
  Register #(.trigger("falling")) register_2 (.D(Data), .en(decoder_1_out1), .clk(CLK), .Q(register_2_q));  // open: clr
  Register #(.trigger("falling")) register_3 (.D(Data), .en(decoder_1_out2), .clk(CLK), .Q(register_3_q));  // open: clr
  Register #(.trigger("falling")) register_4 (.D(Data), .en(decoder_1_out3), .clk(CLK), .Q(register_4_q));  // open: clr
  Register #(.trigger("falling")) register_5 (.D(Data), .en(decoder_1_out4), .clk(CLK), .Q(register_5_q));  // open: clr
  Register #(.trigger("falling")) register_6 (.D(Data), .en(decoder_1_out5), .clk(CLK), .Q(register_6_q));  // open: clr
  Register #(.trigger("falling")) register_7 (.D(Data), .en(decoder_1_out6), .clk(CLK), .Q(register_7_q));  // open: clr
  Register #(.trigger("falling")) register_8 (.D(Data), .en(decoder_1_out7), .clk(CLK), .Q(register_8_q));  // open: clr
  Multiplexer #(.select(3), .width(8)) multiplexer_1 (
    .in0(register_1_q), .in1(register_2_q), .in2(register_3_q), .in3(register_4_q), .in4(register_5_q),
    .in5(register_6_q), .in6(register_7_q), .in7(register_8_q), .out(read_data1), .sel(rs));
  Multiplexer #(.select(3), .width(8)) multiplexer_2 (
    .in0(register_1_q), .in1(register_2_q), .in2(register_3_q), .in3(register_4_q), .in4(register_5_q),
    .in5(register_6_q), .in6(register_7_q), .in7(register_8_q), .out(read_data2), .sel(rt));
endmodule

module CPU (
  output [3:0] out_1,
  output [2:0] out_2,
  output [7:0] out_3,
  output [7:0] out_4,
  output [2:0] out_5,
  output [9:0] out_6,
  output [2:0] out_7,
  output [9:0] out_8,
  output [7:0] out_9,
  output [1:0] out_10,
  output [9:0] out_11
);

  wire clock_1_out, EQ, MR, mux2, MW, WE;
  wire [1:0] mux1;
  wire [2:0] alufunc;
  wire [7:0] Data_Mem_readdata, multiplexer_2_out, multiplexer_3_out, Reg_File_read_data2;
  wire [9:0] imm_ext, Ins_Memory_jump_imm, multiplexer_1_out;

  Clock clock_1 (.out(clock_1_out));
  Multiplexer #(.select(2), .width(10)) multiplexer_1 (
    .in0(out_8), .in1(out_11), .in2(Ins_Memory_jump_imm), .out(multiplexer_1_out), .sel(out_10));  // open: in3
  ProgramCounter PC (.In(multiplexer_1_out), .Clock(clock_1_out), .PC(out_6));
  Adder #(.width(10)) adder_1 (.a(out_6), .b(10'h1), .out(out_8));  // open: cin, cout
  Adder #(.width(10)) adder_2 (.a(imm_ext), .b(out_6), .out(out_11));  // open: cin, cout
  Control_Unit control_unit_1 (
    .Opcode(out_1), .EQ(EQ), .Alufunc(alufunc), .Mux1(mux1), .Mux2(mux2), .WE(WE), .Write(MW), .Read(MR),
    .mux3(out_10));  // open: PCmux, Branch
  Instruction_Memory Ins_Memory (
    .In(out_6), .Opcode(out_1), .Rs(out_2), .Rt(out_5), .Rd(out_7), .Immediate(out_9),
    .Jump_imm(Ins_Memory_jump_imm));
  assign imm_ext = {{2{out_9[7]}}, out_9};  // Bit_Extender bit_extender_1
  Multiplexer #(.select(2), .width(8)) multiplexer_2 (
    .in0(out_3), .in1(Data_Mem_readdata), .in2(out_9), .out(multiplexer_2_out), .sel(mux1));  // open: in3
  Register_File Reg_File (
    .rs(out_2), .rt(out_5), .rd(out_7), .WE(WE), .Data(multiplexer_2_out), .CLK(clock_1_out),
    .read_data1(out_4), .read_data2(Reg_File_read_data2));
  Multiplexer #(.width(8)) multiplexer_3 (.in0(Reg_File_read_data2), .in1(out_9), .out(multiplexer_3_out), .sel(mux2));
  ALU8 ALU_8 (.X(out_4), .Y(multiplexer_3_out), .ALUfunc(alufunc), .RESULT(out_3), .EQ(EQ));
  Data_Memory Data_Mem (
    .Address(out_3), .WE(MW), .RE(MR), .Clock(clock_1_out), .Data(Reg_File_read_data2),
    .ReadData(Data_Mem_readdata));

  // Other names for the same wires on the sheet: branch_imm[9:0] = out_11; imm[7:0] = out_9; mux3[1:0] = out_10;
  //   PC[9:0] = out_6

  // Notes on the sheet:
  //   immediate
  //   opcode
  //   immediate
  //   ALU result
endmodule

module Instruction_Memory (
  input  [9:0] In,
  output [3:0] Opcode,
  output [2:0] Rs,
  output [2:0] Rt,
  output [2:0] Rd,
  output [7:0] Immediate,
  output [9:0] Jump_imm
);

  ROM #(.addrWidth(10), .dataWidth(21)) rom_1 (.addr(In), .data({Opcode, Rs, Rt, Rd[2], Jump_imm[9:8], Immediate}));

  assign Jump_imm[7:0] = Immediate;
  assign Rd[1:0] = Jump_imm[9:8];

  // Notes on the sheet:
  //   contents of rom_1 (hex, n*v repeats v):
  //   60306 60601 6040c 1f700 1f3d00 f70fe 160009 b200
endmodule

// PC
module ProgramCounter (
  input  [9:0] In,
  input  Clock,
  output [9:0] PC
);

  Register #(.trigger("falling"), .width(10)) register_1 (.D(In), .clk(Clock), .Q(PC));  // open: en, clr
endmodule

module Data_Memory (
  input  [7:0] Address,
  input  WE,
  input  RE,
  input  Clock,
  input  [7:0] Data,
  output [7:0] ReadData
);

  RAM #(.asyncread("true"), .trigger("falling")) ram_data (
    .addr(Address), .we(WE), .oe(RE), .clk(Clock), .din(Data), .dout(ReadData));
endmodule

module Control_Unit (
  input  [3:0] Opcode,
  input  EQ,
  output [2:0] Alufunc,
  output [1:0] Mux1,
  output Mux2,
  output WE,
  output Write,
  output Read,
  output [1:0] PCmux,
  output [1:0] mux3,
  output Branch
);

  wire and_1_out, and_2_out, and_3_out, and_6_out, and_7_out, and_8_out, and_9_out, and_10_out, not_1_out,
       not_2_out, not_3_out, not_4_out, not_5_out, not_6_out, not_7_out, not_8_out, not_9_out, not_10_out,
       not_11_out, not_12_out, not_13_out, not_14_out, not_15_out, not_16_out, not_17_out, not_18_out,
       not_19_out;
  wire [1:0] bit_extender_1_out;

  not not_1 (not_1_out, Opcode[3]);
  not not_2 (not_2_out, Opcode[2]);
  not not_3 (not_3_out, Opcode[2]);
  not not_4 (not_4_out, Opcode[1]);
  not not_5 (not_5_out, Opcode[3]);
  not not_6 (not_6_out, EQ);
  not not_7 (not_7_out, Opcode[2]);
  not not_8 (not_8_out, Opcode[2]);
  not not_9 (not_9_out, Opcode[1]);
  and and_1 (and_1_out, not_9_out, not_10_out);
  not not_10 (not_10_out, Opcode[0]);
  and and_2 (and_2_out, Opcode[3], Opcode[2]);
  not not_11 (not_11_out, Opcode[3]);
  not not_12 (not_12_out, Opcode[2]);
  and and_3 (and_3_out, not_11_out, not_12_out, Opcode[0]);
  and and_4 (Write, Opcode[1], not_13_out);
  not not_13 (not_13_out, Opcode[0]);
  not not_14 (not_14_out, Opcode[2]);
  not not_15 (not_15_out, Opcode[1]);
  and and_5 (Read, not_14_out, not_15_out, Opcode[0]);
  and PCmux_0 (PCmux[0], not_1_out, Opcode[2], Opcode[0]);
  and PCmux_1 (PCmux[1], Opcode[3], not_2_out, Opcode[0]);
  and and_6 (and_6_out, Opcode[3], not_3_out, Opcode[0]);
  and and_7 (and_7_out, Opcode[2], not_4_out, Opcode[0], EQ);
  and and_8 (and_8_out, not_5_out, Opcode[2], Opcode[1], not_6_out);
  not not_16 (not_16_out, Opcode[1]);
  not not_17 (not_17_out, Opcode[1]);
  not not_18 (not_18_out, Opcode[1]);
  not not_19 (not_19_out, Opcode[3]);
  and and_9 (and_9_out, not_7_out, Opcode[0]);
  and and_10 (and_10_out, not_8_out, Opcode[1]);
  and Alufunc_0 (Alufunc[0], Opcode[2], not_16_out);
  and Alufunc_1 (Alufunc[1], Opcode[3], not_17_out);
  and Alufunc_2 (Alufunc[2], Opcode[2], Opcode[0]);
  and Mux1_0 (Mux1[0], not_18_out, Opcode[0]);
  and Mux1_1 (Mux1[1], not_19_out, Opcode[1]);
  or or_1 (Branch, and_6_out, and_7_out, and_8_out);
  or or_2 (Mux2, and_9_out, and_10_out);
  or or_3 (WE, and_1_out, and_2_out, and_3_out);
  assign bit_extender_1_out = {{1{Branch}}, Branch};  // Bit_Extender bit_extender_1
  assign mux3 = PCmux & bit_extender_1_out;  // AND_Gate and_11, 2 bits wide

  // Other names for the same wires on the sheet: op0 = Opcode[0]; op1 = Opcode[1]; op2 = Opcode[2]; op3 = Opcode[3]
endmodule
